# Fritzing sketch I-tub_라즈베리파이_회로도 (saved by Fritzing 0.9.3b)
breadboards: 1

parts:
  Raspberry_Pi_1 = Raspberry Pi 3 [part_number=RPI-3-V1.2]
  U1 = Nokia 6100 Color LCD [package=nokia6100_lcd]
  U2 = L9110 H-bridge module [part_number="L9110 H-bridge"]
  module1 = PCF8591
  M1 = DC Motor
  M2 = DC Motor
  부품1 = Soil Moisture Sensor
  DS1 = DS18B20 1-Wire Temperature Sensor [part_number=DS18B20]
  J1 = Basic Servo

nets:
  N1: Raspberry_Pi_1.GPIO2, module1.SDA
  N2: Raspberry_Pi_1.GPIO3, module1.SCL
  N3: Raspberry_Pi_1.GPIO4, DS1.DQ
  GND: Raspberry_Pi_1.GND, U1.GND, U2.GND, module1.GND, 부품1.GND, DS1.GND, J1.gnd
  N4: Raspberry_Pi_1.GPIO22, J1.pulse
  N5: Raspberry_Pi_1.GPIO5, U2.B-IA
  N6: Raspberry_Pi_1.GPIO6, U2.B-IB
  N7: Raspberry_Pi_1.GPIO13, U2.A-IA
  N8: Raspberry_Pi_1.GPIO19, U2.A-IB
  VCC: Raspberry_Pi_1.5V, U1.VLED, U2.VCC, module1.VCC, 부품1.VCC, DS1.VDD, J1.vcc
  N9: U2.MOTOR_A-A, M2.pin_2
  N10: U2.MOTOR_A-B, M2.pin_1
  N11: U2.MOTOR_B-A, M1.pin_2
  N12: U2.MOTOR_B-B, M1.pin_1
  N13: module1.AO, 부품1.SIG

custom parts:
  PCF8591: PCF8591 ADC module for SunFounder Sensor Kit
